// Logisim project ULA_final3.circ as structural Verilog: 7 circuits, main circuit celula
module celula (
  input  A,
  input  B,
  input  [2:0] in_3,
  input  in_4,
  output out_5,
  output out_6
);

  wire and_1_out, and_2_out, nand_1_out, nor_1_out, or_1_out, somador_1_out_5, somador_1_s,
       subtrator_1_out_5, subtrator_1_s, xnor_1_out, xor_1_out;

  and and_1 (and_1_out, A, B);
  or or_1 (or_1_out, A, B);
  nand nand_1 (nand_1_out, A, B);
  nor nor_1 (nor_1_out, A, B);
  xor xor_1 (xor_1_out, A, B);
  xnor xnor_1 (xnor_1_out, A, B);
  Somador somador_1 (.A(A), .B(B), .C(in_4), .out_5(somador_1_out_5), .S(somador_1_s));
  Subtrator subtrator_1 (.A(A), .B(B), .C(in_4), .out_5(subtrator_1_out_5), .S(subtrator_1_s));
  Multiplexer #(.select(3), .enable("false")) multiplexer_1 (
    .in0(and_1_out), .in1(or_1_out), .in2(nand_1_out), .in3(nor_1_out), .in4(xor_1_out), .in5(xnor_1_out),
    .in6(somador_1_s), .in7(subtrator_1_s), .out(out_5), .sel(in_3));
  and and_2 (and_2_out, in_3[2], in_3[1], in_3[0]);
  Multiplexer #(.enable("false")) multiplexer_2 (
    .in0(somador_1_out_5), .in1(subtrator_1_out_5), .out(out_6), .sel(and_2_out));
  SOMADOR2 somador2_1 ();  // open: A, out_3, B
endmodule

module ULA (
  input  [2:0] SELETOR,
  input  [7:0] A,
  input  [7:0] B,
  input  [7:0] in_4,
  input  [7:0] in_5,
  output OVERFLOW,
  output [7:0] out_7,
  output [7:0] out_8,
  output [7:0] out_9
);

  wire celula_1_out_6, celula_2_out_6, celula_3_out_6, celula_4_out_6, celula_5_out_6, celula_6_out_6,
       celula_7_out_6, decodificador_1_a_2, decodificador_1_b_2, decodificador_1_c_2, decodificador_1_d_2,
       decodificador_1_e, decodificador_1_f, decodificador_1_g, decodificador_2_a_2, decodificador_2_b_2,
       decodificador_2_c_2, decodificador_2_d_2, decodificador_2_e, decodificador_2_f, decodificador_2_g,
       decodificador_3_a_2, decodificador_3_b_2, decodificador_3_c_2, decodificador_3_d_2, decodificador_3_e,
       decodificador_3_f, decodificador_3_g;
  wire [7:0] celula_1_out_5, divider_1_rem;

  celula celula_1 (.A(A[0]), .B(B[0]), .in_4(1'b0), .in_3(SELETOR), .out_5(celula_1_out_5[0]), .out_6(celula_1_out_6));
  Divider divider_1 (
    .a(celula_1_out_5), .b(in_4), .out({{4{out_7[7]}}, out_7[3:0]}), .rem(divider_1_rem));  // open: upper
  celula celula_2 (
    .A(A[1]), .B(B[1]), .in_4(celula_1_out_6), .in_3(SELETOR), .out_5(celula_1_out_5[1]),
    .out_6(celula_2_out_6));
  _7_Segment_Display u_7_segment_display_1 (
    .g(decodificador_1_g), .f(decodificador_1_f), .a(decodificador_1_a_2), .b(decodificador_1_b_2),
    .e(decodificador_1_e), .d(decodificador_1_d_2), .c(decodificador_1_c_2));  // open: dp
  Divider divider_2 (
    .a(divider_1_rem), .b(in_5), .out({{4{out_8[7]}}, out_8[3:0]}), .rem({{4{out_9[7]}}, out_9[3:0]}));  // open: upper
  celula celula_3 (
    .A(A[2]), .B(B[2]), .in_4(celula_2_out_6), .in_3(SELETOR), .out_5(celula_1_out_5[2]),
    .out_6(celula_3_out_6));
  Decodificador decodificador_1 (
    .A(out_7[3]), .B(out_7[2]), .C(out_7[1]), .D(out_7[0]), .g(decodificador_1_g), .f(decodificador_1_f),
    .a_2(decodificador_1_a_2), .b_2(decodificador_1_b_2), .c_2(decodificador_1_c_2),
    .d_2(decodificador_1_d_2), .e(decodificador_1_e));
  celula celula_4 (
    .A(A[3]), .B(B[3]), .in_4(celula_3_out_6), .in_3(SELETOR), .out_5(celula_1_out_5[3]),
    .out_6(celula_4_out_6));
  _7_Segment_Display u_7_segment_display_2 (
    .g(decodificador_2_g), .f(decodificador_2_f), .a(decodificador_2_a_2), .b(decodificador_2_b_2),
    .e(decodificador_2_e), .d(decodificador_2_d_2), .c(decodificador_2_c_2));  // open: dp
  celula celula_5 (
    .A(A[4]), .B(B[4]), .in_4(celula_4_out_6), .in_3(SELETOR), .out_5(celula_1_out_5[4]),
    .out_6(celula_5_out_6));
  Decodificador decodificador_2 (
    .A(out_8[3]), .B(out_8[2]), .C(out_8[1]), .D(out_8[0]), .g(decodificador_2_g), .f(decodificador_2_f),
    .a_2(decodificador_2_a_2), .b_2(decodificador_2_b_2), .c_2(decodificador_2_c_2),
    .d_2(decodificador_2_d_2), .e(decodificador_2_e));
  celula celula_6 (
    .A(A[5]), .B(B[5]), .in_4(celula_5_out_6), .in_3(SELETOR), .out_5(celula_1_out_5[5]),
    .out_6(celula_6_out_6));
  Decodificador decodificador_3 (
    .A(out_9[3]), .B(out_9[2]), .C(out_9[1]), .D(out_9[0]), .g(decodificador_3_g), .f(decodificador_3_f),
    .a_2(decodificador_3_a_2), .b_2(decodificador_3_b_2), .c_2(decodificador_3_c_2),
    .d_2(decodificador_3_d_2), .e(decodificador_3_e));
  _7_Segment_Display u_7_segment_display_3 (
    .g(decodificador_3_g), .f(decodificador_3_f), .a(decodificador_3_a_2), .b(decodificador_3_b_2),
    .e(decodificador_3_e), .d(decodificador_3_d_2), .c(decodificador_3_c_2));  // open: dp
  celula celula_7 (
    .A(A[6]), .B(B[6]), .in_4(celula_6_out_6), .in_3(SELETOR), .out_5(celula_1_out_5[6]),
    .out_6(celula_7_out_6));
  celula celula_8 (
    .A(A[7]), .B(B[7]), .in_4(celula_7_out_6), .in_3(SELETOR), .out_5(celula_1_out_5[7]), .out_6(OVERFLOW));

  assign out_7[6:4] = {3{out_7[7]}};
  assign out_8[6:4] = {3{out_8[7]}};
  assign out_9[6:4] = {3{out_9[7]}};

  // Notes on the sheet:
  //   Divisão por "100"
  //   Divisão por "10"
endmodule

module Somador (
  input  C,
  input  A,
  input  B,
  output S,
  output out_5
);

  wire and_1_out, and_2_out, and_3_out, xor_1_out;

  xor xor_1 (xor_1_out, B, C);
  and and_1 (and_1_out, B, C);
  and and_2 (and_2_out, B, A);
  and and_3 (and_3_out, C, A);
  xor xor_2 (S, A, xor_1_out);
  or or_1 (out_5, and_1_out, and_2_out, and_3_out);
endmodule

module Subtrator (
  input  C,
  input  A,
  input  B,
  output S,
  output out_5
);

  wire and_1_out, and_2_out, and_3_out, not_1_out, xor_1_out;

  not not_1 (not_1_out, A);
  xor xor_1 (xor_1_out, B, C);
  and and_1 (and_1_out, B, C);
  and and_2 (and_2_out, B, not_1_out);
  and and_3 (and_3_out, C, not_1_out);
  xor xor_2 (S, A, xor_1_out);
  or or_1 (out_5, and_1_out, and_2_out, and_3_out);
endmodule

module Decodificador (
  input  A,
  input  B,
  input  C,
  input  D,
  output c_2,
  output d_2,
  output e,
  output g,
  output f,
  output a_2,
  output b_2
);

  wire and_1_out, and_2_out, and_3_out, and_4_out, and_5_out, and_6_out, and_7_out, and_8_out, and_9_out,
       and_10_out, and_11_out, and_12_out, and_13_out, and_14_out, and_15_out, and_16_out, not_1_out,
       not_2_out, not_3_out;

  not not_1 (not_1_out, B);
  not not_2 (not_2_out, C);
  not not_3 (not_3_out, D);
  and and_1 (and_1_out, B, D);
  and and_2 (and_2_out, not_1_out, not_3_out);
  and and_3 (and_3_out, C, D);
  and and_4 (and_4_out, not_2_out, not_3_out);
  and and_5 (and_5_out, not_1_out, not_3_out);
  and and_6 (and_6_out, not_1_out, C);
  and and_7 (and_7_out, C, not_3_out);
  and and_8 (and_8_out, B, not_2_out, D);
  and and_9 (and_9_out, not_1_out, not_3_out);
  and and_10 (and_10_out, C, not_3_out);
  and and_11 (and_11_out, not_2_out, not_3_out);
  and and_12 (and_12_out, B, not_2_out);
  and and_13 (and_13_out, B, not_3_out);
  and and_14 (and_14_out, B, not_2_out);
  and and_15 (and_15_out, not_1_out, C);
  and and_16 (and_16_out, C, not_3_out);
  or or_1 (a_2, A, and_1_out, C, and_2_out);
  or or_2 (b_2, not_1_out, and_3_out, and_4_out);
  or or_3 (c_2, B, not_2_out, D);
  or or_4 (d_2, A, and_5_out, and_6_out, and_7_out, and_8_out);
  or or_5 (e, and_9_out, and_10_out);
  or or_6 (f, A, and_11_out, and_12_out, and_13_out);
  or or_7 (g, A, and_14_out, and_15_out, and_16_out);
endmodule

module SOMADOR2 (
  input  [7:0] B,
  input  [7:0] A,
  output [7:0] out_3
);

  wire somador_1_out_5, somador_2_out_5, somador_3_out_5, somador_4_out_5, somador_5_out_5, somador_6_out_5,
       somador_7_out_5;

  Somador somador_1 (.A(A[0]), .B(B[0]), .C(1'b0), .out_5(somador_1_out_5), .S(out_3[0]));
  Somador somador_2 (.A(A[1]), .B(B[1]), .C(somador_1_out_5), .out_5(somador_2_out_5), .S(out_3[1]));
  Somador somador_3 (.A(A[2]), .B(B[2]), .C(somador_2_out_5), .out_5(somador_3_out_5), .S(out_3[2]));
  Somador somador_4 (.A(A[3]), .B(B[3]), .C(somador_3_out_5), .out_5(somador_4_out_5), .S(out_3[3]));
  Somador somador_5 (.A(A[4]), .B(B[4]), .C(somador_4_out_5), .out_5(somador_5_out_5), .S(out_3[4]));
  Somador somador_6 (.A(A[5]), .B(B[5]), .C(somador_5_out_5), .out_5(somador_6_out_5), .S(out_3[5]));
  Somador somador_7 (.A(A[6]), .B(B[6]), .C(somador_6_out_5), .out_5(somador_7_out_5), .S(out_3[6]));
  Somador somador_8 (.A(A[7]), .B(B[7]), .C(somador_7_out_5), .S(out_3[7]));  // open: out_5
endmodule

module subtrator2 (
  input  [7:0] B,
  input  [7:0] A,
  output [7:0] out_3
);

  wire subtrator_1_out_5, subtrator_2_out_5, subtrator_3_out_5, subtrator_4_out_5, subtrator_5_out_5,
       subtrator_6_out_5, subtrator_7_out_5;

  Subtrator subtrator_1 (.A(A[0]), .B(B[0]), .C(1'b0), .out_5(subtrator_1_out_5), .S(out_3[0]));
  Subtrator subtrator_2 (.A(A[1]), .B(B[1]), .C(subtrator_1_out_5), .out_5(subtrator_2_out_5), .S(out_3[1]));
  Subtrator subtrator_3 (.A(A[2]), .B(B[2]), .C(subtrator_2_out_5), .out_5(subtrator_3_out_5), .S(out_3[2]));
  Subtrator subtrator_4 (.A(A[3]), .B(B[3]), .C(subtrator_3_out_5), .out_5(subtrator_4_out_5), .S(out_3[3]));
  Subtrator subtrator_5 (.A(A[4]), .B(B[4]), .C(subtrator_4_out_5), .out_5(subtrator_5_out_5), .S(out_3[4]));
  Subtrator subtrator_6 (.A(A[5]), .B(B[5]), .C(subtrator_5_out_5), .out_5(subtrator_6_out_5), .S(out_3[5]));
  Subtrator subtrator_7 (.A(A[6]), .B(B[6]), .C(subtrator_6_out_5), .out_5(subtrator_7_out_5), .S(out_3[6]));
  Subtrator subtrator_8 (.A(A[7]), .B(B[7]), .C(subtrator_7_out_5), .S(out_3[7]));  // open: out_5
endmodule
